# Fritzing sketch mqtt-pager-fritzing (saved by Fritzing 0.9.3b)
breadboards: 1

parts:
  U1 = ESP32-38PinWide [part_number=ESP32-38PinWide]
  R1 = Resistor [tolerance=±5% resistance=470 package=THT]
  LED1 = LED - 5mm [color="Red (633nm)" package="5 mm [THT]"]
  S1 = Pushbutton [package="[THT]"]
  R2 = Resistor [tolerance=±5% resistance=4.7k package=THT]
  J1 = Piezo Speaker

nets:
  N1: U1.GPIO34, S1.Pin_1, S1.Pin_2, R2.Pin_1
  N2: U1.GPIO12, J1.pin2
  N3: U1.GPIO11, R2.Pin_0
  N4: U1.VIN, LED1.cathode, S1.Pin_3, S1.Pin_4, J1.pin1
  N5: U1.GPIO23, R1.Pin_0
  N6: R1.Pin_1, LED1.anode

custom parts:
  ESP32-38PinWide: Generic 38-Pin ESP32 with wide format (only access to one side of pins on a breadboard) based on Stephen Lilley's HiLetgo ESP-WROOM-32 ESP32 ESP-32S Development Board.
